# Fritzing sketch TempHumESP01 (saved by Fritzing 0.9.4b)
perfboards: 1

parts:
  J1 = JST-B3P-VH [part_number=JST-B3P-VH package=THT]  # not connected
  J2 = JST-03JQ-BT [part_number=JST-JQ-BT package=THT]  # not connected
  J3 = female pin header, 4 pins [form="♀ (female)"]
  J4 = female pin header, 4 pins [form="♀ (female)"]
  J6 = female pin header, 3 pins [form="♀ (female)"]
  J7 = female pin header, 2 pins [form="♀ (female)"]
  J5 = female pin header, 3 pins [form="♀ (female)"]

nets:
  N1: J3.pin2, J3.pin4, J6.pin2, J5.pin1
  N2: J4.pin1, J6.pin1, J7.pin1, J5.pin3
  N3: J4.pin3, J5.pin2
  N4: J6.pin3, J7.pin2
